// Logisim project my_cpu.circ as structural Verilog: 1 circuit, main circuit main
module main (
  input  [7:0] A1,
  input  [7:0] B1,
  input  [7:0] A7,
  input  [7:0] A8,
  input  [7:0] A2,
  input  [7:0] A3,
  input  [7:0] B3,
  input  [7:0] A4,
  input  [7:0] B4,
  input  [7:0] A6,
  input  [7:0] A5,
  input  [7:0] A9,
  input  [7:0] B9,
  input  [7:0] in_14,
  input  [3:0] Opcode,
  input  [7:0] in_16,
  input  [7:0] in_17,
  input  [7:0] in_18,
  input  [7:0] in_19,
  output [7:0] out_20,
  output out_21,
  output out_22,
  output out_23
);

  wire button_1_out, button_2_out, button_3_out, button_4_out;
  wire [7:0] A_q, adder_1_out, adder_2_out, adder_3_out, and_1_out, B_q, not_1_out, or_1_out, shifter_1_out,
       shifter_2_out, subtractor_1_out, subtractor_2_out, xor_1_out;

  Adder adder_1 (.a(A1), .b(B1), .out(adder_1_out));  // open: cin, cout
  Adder adder_2 (.a(A7), .b(8'h1), .out(adder_2_out));  // open: cin, cout
  Subtractor subtractor_1 (.a(A8), .b(8'h1), .out(subtractor_1_out));  // open: bin, bout
  assign not_1_out = ~A2;  // NOT_Gate not_1, 8 bits wide
  assign and_1_out = A3 & B3;  // AND_Gate and_1, 8 bits wide
  assign or_1_out = A4 | B4;  // OR_Gate or_1, 8 bits wide
  Shifter shifter_1 (.in(A6), .\dist (3'b001), .out(shifter_1_out));
  Shifter #(.shift("lr")) shifter_2 (.in(A5), .\dist (3'b001), .out(shifter_2_out));
  Subtractor subtractor_2 (.a(in_14), .b(in_16), .out(subtractor_2_out));  // open: bin, bout
  assign xor_1_out = in_17 ^ in_18;  // XOR_Gate xor_1, 8 bits wide
  Comparator comparator_1 (.a(A9), .b(B9), .gt(out_21), .eq(out_22), .lt(out_23));
  Adder adder_3 (.a(A_q), .b(B_q), .out(adder_3_out));  // open: cin, cout
  Multiplexer #(.disabled("Z"), .enable("true"), .select(4), .width(8)) multiplexer_1 (
    .in0(adder_1_out), .in1(adder_2_out), .in2(subtractor_1_out), .in3(not_1_out), .in4(and_1_out),
    .in5(or_1_out), .in6(shifter_1_out), .in7(shifter_2_out), .in8(subtractor_2_out), .in9(xor_1_out),
    .in10(in_19), .in11({8{1'b0}}), .in12({8{1'b1}}), .in13(adder_3_out), .out(out_20), .sel(Opcode),
    .en(1'b1));  // open: in14, in15
  Register A (.D(out_20), .en(button_1_out), .clk(button_2_out), .Q(A_q));  // open: clr
  Button button_1 (.out(button_1_out));
  Button button_2 (.out(button_2_out));
  Register B (.D(out_20), .en(button_3_out), .clk(button_4_out), .Q(B_q));  // open: clr
  Button button_3 (.out(button_3_out));
  Button button_4 (.out(button_4_out));
endmodule
